# Fritzing sketch ButtonInputPullupResistor (saved by Fritzing 0.9.3b)
breadboards: 1

parts:
  Parts1 = SparkFun RedBoard [part_number=DEV-12757]
  S1 = Momentary Switch [package=ksa_sealed_tac_switch]
  R1 = Resistor [tolerance=±5% resistance=1k package="0805 [SMD]"]
  R1_2 = Resistor [tolerance=±5% resistance=10k package="0402 [SMD]"]

nets:
  N1: Parts1.D2, S1.2
  N2: Parts1.5V, R1.Pin_1, R1_2.Pin_1
  N3: Parts1.GND, S1.1
  N4: S1.3, R1.Pin_0, R1_2.Pin_0

custom parts:
  SparkFun RedBoard: At SparkFun we use many Arduinos and we’re always looking for the simplest, most stable one. Each board is a bit different and no one board has everything we want, so we decided to make our own version that combines all our favorite features. The RedBoard combines the simplicity of the UNO’s Optiboot bootloader (which is used in the Pro series), the stability of the FTDI (which we all missed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
