# Fritzing sketch Series1 (saved by Fritzing 0.9.4)
circuit board: 8.46667cm x 5.64444cm
breadboards: 2

parts:
  R1 = Resistor [tolerance=±5% resistance=68 package=THT]
  LED1 = LED - 5mm [color="Red (633nm)" package="5 mm [THT]"]
  LED2 = LED - 5mm [color="Red (633nm)" package="5 mm [THT]"]
  Part1 = Arduino Uno (Rev3)
  VCC1 = Battery block 9V  # not connected
  LED3 = smd LED [color="Red (633nm)" package="1206 [SMD]"]
  LED4 = smd LED [color="Red (633nm)" package="1206 [SMD]"]
  LED5 = smd LED [color="Red (633nm)" package="1206 [SMD]"]
  LED6 = smd LED [color="Red (633nm)" package="1206 [SMD]"]
  R2 = Resistor [tolerance=±5% resistance=220 package=THT]

nets:
  N1: R1.Pin_0, LED2.cathode
  N2: R1.Pin_1, Part1.GND
  N3: LED1.cathode, LED2.anode
  N4: LED1.anode, Part1.D6_PWM
  N5: LED3.cathode, LED4.anode
  N6: LED4.cathode, LED5.anode
  N7: LED5.cathode, LED6.anode
  N8: LED6.cathode, R2.Pin_0
