# Fritzing sketch simple2RadioHookup (saved by Fritzing 0.9.3b)

parts:
  Part1 = NRF24L01+ Breakout Board
  C1 = Electrolytic Capacitor [capacitance=4.7µF package="100 mil [THT, electrolytic]"]
  Part3 = Arduino Nano (Rev3.0) (ICSP)
  Part4 = NRF24L01+ Breakout Board
  C2 = Electrolytic Capacitor [capacitance=4.7µF package="100 mil [THT, electrolytic]"]
  Part5 = Arduino Nano (Rev3.0) (ICSP)
  S1 = Momentary Switch [package=ksa_sealed_tac_switch]  # not connected
  R1 = Resistor [tolerance=±5% resistance=10k package="2512 [SMD]"]  # not connected
  R2 = Resistor [tolerance=±5% resistance=330 package="2512 [SMD]"]  # not connected
  LED1 = LED - 5mm [color="Red (633nm)" package="5 mm [THT]"]  # not connected

nets:
  GND: Part1.GND, C1.-, Part3.GND, Part4.GND, C2.-, Part5.GND
  VCC: Part1.VCC, C1.+, Part3.3V3
  N1: Part1.CE, Part3.D9
  N2: Part1.CS, Part3.D10
  N3: Part1.SCK, Part3.D13/SCK
  N4: Part1.MOSI, Part3.D11/MOSI
  N5: Part1.MISO, Part3.D12/MISO
  VIN: Part3.VIN, Part5.VIN
  VCC_2: Part4.VCC, C2.+, Part5.3V3
  N6: Part4.CE, Part5.D9
  N7: Part4.CS, Part5.D10
  N8: Part4.SCK, Part5.D13/SCK
  N9: Part4.MOSI, Part5.D11/MOSI
  N10: Part4.MISO, Part5.D12/MISO

notes:
  Connect Vin pins and GND on both Arduinos so they can share a single power source
