# Fritzing sketch radioHookup (saved by Fritzing 0.9.3b)

parts:
  Part1 = NRF24L01+ Breakout Board
  Part2 = Arduino Uno (Rev3) - ICSP
  C1 = Electrolytic Capacitor [capacitance=4.7µF package="100 mil [THT, electrolytic]"]

nets:
  GND: Part1.GND, Part2.GND, C1.-
  VCC: Part1.VCC, Part2.3V3, C1.+
  N1: Part1.CE, Part2.D9_PWM
  N2: Part1.CS, Part2.D10_PWM/SS
  N3: Part1.SCK, Part2.D13/SCK
  N4: Part1.MOSI, Part2.D11_PWM/MOSI
  N5: Part1.MISO, Part2.D12/MISO
